# Fritzing sketch schematic.diagram (saved by Fritzing 0.9.2b)
breadboards: 1

parts:
  元件1 = Arduino Leonardo (Rev3b)
  R1 = Resistor [tolerance=±5% resistance=220 package=THT]  # not connected
  S2 = Momentary Switch [package=ksa_sealed_tac_switch]
  S3 = Momentary Switch [package=ksa_sealed_tac_switch]
  R2 = Resistor [tolerance=±5% resistance=220 package=THT]
  T1 = LM35 Temperature Sensor [package="TO92 [THT]"]

nets:
  N1: 元件1.D2/SDA, T1.Vout
  N2: 元件1.5V, R2.Pin_0
  N3: 元件1.D8/A8, S3.4, R2.Pin_1
  N4: 元件1.D9_PWM/A9, S2.4
  N5: 元件1.GND, S2.2, S3.2

notes:
  实际为光电开关
